# Fritzing sketch NFC_reader_test1 (saved by Fritzing 0.9.10b)
breadboards: 1

parts:
  A1 = Esp32-c3 super mini
  D1 = Schottky Diode [part_number=1N5817 package="300 mil [THT]"]
  V2 = DC Power [voltage=4.2V]
  Composant2 = RFID-RC522-v3  # not connected

nets:
  3.3V: A1.Pin_14, D1.cathode
  GND: A1.Pin_15, V2.V-
  N1: D1.anode, V2.V+

notes:
  zf240510.1452
  zf240510.1521

custom parts:
  Esp32-c3 super mini: ESP32-C3 Development Board ESP32 SuperMini Development Board ESP32 Development Board WiFi Bluetooth.
  RFID-RC522-v3: A simple China made RFID-RC522 Reader (6x4 cm); do check the pin labels, as this is a MFRC522 based clone.
